# Fritzing sketch A2 (saved by Fritzing 0.9.3b)
breadboards: 2
perfboards: 1

parts:
  Teensy1 = Teensy 2.0
  元件1 = Bluetooth HC-05 Macho
  Teensy2 = Teensy 2.0
  元件2 = Bluetooth HC-05 Macho
  Q2 = PNP-Transistor [package="TO92 [THT]"]
  R1 = Resistor [tolerance=±5% resistance=220 package=THT]
  M1 = DC Motor
  U2 = LCD-16X2 [package=lcd-8x2]
  D1 = SOLAR-IXYS [package=solarbit-12x1]
  Teensy3 = Teensy 2.0  # not connected
  元件4 = Bluetooth HC-05 Macho  # not connected
  元件5 = Soil Moisture Sensor  # not connected
  U4 = LIPO-2000mAh [package=lipo-2000]  # not connected
  Grove1 = Grove Temperature Sensor  # not connected
  元件3 = PowerBoost 500 Charger
  U3 = Voltage Regulator - Variable [package="TO220 [THT]"]
  元件6 = Ludus ProtoShield  # not connected

nets:
  GND: Teensy1.GND, 元件1.GND, R1.Pin_1
  N1: Teensy1.D2, 元件1.TXD
  N2: Teensy1.D3, 元件1.RXD
  N3: Teensy1.B6, Q2.B, R1.Pin_0
  VCC: Teensy1.VCC, 元件1.VCC
  GND_2: Teensy2.GND, 元件2.GND
  N4: Teensy2.D2, 元件2.TXD
  N5: Teensy2.D3, 元件2.RXD
  N6: Teensy2.D6, U2.RS
  N7: Teensy2.D7, U2.E
  N8: Teensy2.B4, U2.DB1
  N9: Teensy2.B5, U2.DB3
  N10: Teensy2.B6, U2.DB5
  N11: Teensy2.F7, U2.DB7
  N12: Teensy2.F6, U2.K
  VCC_2: Teensy2.VCC, 元件2.VCC
  N13: Q2.C, M1.pin_1
  N14: D1.A, 元件3.GND
  N15: D1.C, U3.IN
  N16: 元件3.USB, U3.ADJ
